# Fritzing sketch fritzing-arduino-rpi-read-ldr (saved by Fritzing 0.9.3b)
breadboards: 1

parts:
  Parça1 = Arduino Uno (Rev3) - ICSP
  Raspberry_Pi_1 = Raspberry Pi 3 [part_number=RPI-3-V1.2]  # not connected
  R1 = Resistor [tolerance=±5% resistance=10k package="1206 [SMD]"]
  R2 = Photocell (LDR) [package=THT]
  LED1 = smd LED [color="Red (633nm)" package="0805 [SMD]"]

nets:
  N1: Parça1.A0, R1.Pin_0, R2.pin_1
  N2: Parça1.D7, LED1.cathode
  N3: Parça1.5V, R1.Pin_1
  N4: Parça1.GND, R2.pin_0, LED1.anode
