# Fritzing sketch arduino-rpi-uart-level-resistors (saved by Fritzing 0.9.3b)
breadboards: 1

parts:
  Parça1 = Arduino Uno (Rev3) - ICSP
  Raspberry_Pi_1 = Raspberry Pi 3 [part_number=RPI-3-V1.2]
  R1 = Resistor [tolerance=±5% resistance=270 package="2010 [SMD]"]
  R2 = Resistor [tolerance=±5% resistance=470 package=THT]

nets:
  GND: Parça1.GND, Raspberry_Pi_1.GND, R2.Pin_1
  N1: Parça1.D0/RX, Raspberry_Pi_1.GIPO14
  N2: Parça1.D1/TX, R1.Pin_0
  N3: Raspberry_Pi_1.GIPO15, R1.Pin_1, R2.Pin_0
