# Fritzing sketch arduino_i2c (saved by Fritzing 0.9.3b)
breadboards: 1

parts:
  Parça1 = Arduino Uno (Rev3) - ICSP
  Parça2 = Arduino Uno (Rev3) - ICSP
  Raspberry_Pi_1 = Raspberry Pi 3 [part_number=RPI-3-V1.2]  # not connected
  LED2 = LED - 3mm [color="Red (633nm)" package="3 mm [THT]"]
  R1 = Photocell (LDR) [package=THT]
  R2 = Resistor [tolerance=±5% resistance=10k package="0402 [SMD]"]
  LED3 = LED - 3mm [color="Red (633nm)" package="3 mm [THT]"]
  R3 = Photocell (LDR) [package=THT]
  R4 = Resistor [tolerance=±5% resistance=10k package="0402 [SMD]"]

nets:
  N1: Parça1.A0, R3.pin_1, R4.Pin_0
  GND: Parça1.GND, Parça2.GND, LED2.cathode, R2.Pin_1, LED3.cathode, R4.Pin_1
  N2: Parça1.A4/SDA, Parça2.A4/SDA
  N3: Parça1.A5/SCL, Parça2.A5/SCL
  N4: Parça1.D2, LED3.anode
  N5: Parça1.5V, R3.pin_0
  N6: Parça2.A0, R1.pin_1, R2.Pin_0
  N7: Parça2.D2, LED2.anode
  N8: Parça2.5V, R1.pin_0

notes:
  I2C Adres 0x5E
  I2C Adres 0x6E
